# Fritzing sketch schematic (saved by Fritzing 0.9.3b)
breadboards: 1

parts:
  arduino_micro = Arduino Micro (Rev3)
  eeprom = IC, DIP package, 8 pins [chip_label=24C65]
  oled = Grove OLED 128x96
  btn_prev = Pushbutton [package="[THT]"]
  btn_next = Pushbutton [package="[THT]"]
  btn_sel = Pushbutton [package="[THT]"]

nets:
  GND: arduino_micro.GND, eeprom.pin1, eeprom.pin2, eeprom.pin3, eeprom.pin4, eeprom.pin7, oled.GND, btn_prev.Pin_1, btn_prev.Pin_2, btn_next.Pin_1, btn_next.Pin_2, btn_sel.Pin_1, btn_sel.Pin_2
  N1: arduino_micro.D2/SDA, eeprom.pin5, oled.SDA
  N2: arduino_micro.D3/SCL, eeprom.pin6, oled.SCL
  N3: arduino_micro.D6_PWM/A7, btn_sel.Pin_3, btn_sel.Pin_4
  N4: arduino_micro.D7, btn_next.Pin_3, btn_next.Pin_4
  N5: arduino_micro.D8_PWM/A8, btn_prev.Pin_3, btn_prev.Pin_4
  N6: arduino_micro.5V, eeprom.pin8
